# Fritzing sketch Raspberry (saved by Fritzing 0.9.3b)

parts:
  Raspberry_Pi_1 = Raspberry Pi 3 [part_number=RPI-3-V1.2]
  Bauteil1 = NRF24L01+ Breakout Board
  C1 = Capacitor Polarized [package=cpol-radial-100uf-25v]

nets:
  3V3: Raspberry_Pi_1.3v3, Bauteil1.VCC, C1.+
  N1: Raspberry_Pi_1.GIPO22, Bauteil1.CE
  N2: Raspberry_Pi_1.GIPO10, Bauteil1.MOSI
  N3: Raspberry_Pi_1.GIPO9, Bauteil1.MISO
  N4: Raspberry_Pi_1.GIPO11, Bauteil1.SCK
  N5: Raspberry_Pi_1.GIPO8, Bauteil1.CS
  GND: Raspberry_Pi_1.GND, Bauteil1.GND, C1.-
