# Fritzing sketch ddtinypir (saved by Fritzing 0.9.3b)
breadboards: 1

parts:
  U2 = ATTiny84 [package=dip]
  R1 = Resistor [tolerance=±5% resistance=220 package=THT]
  BAT1 = Battery Holders [package=battery-aa]
  Bauteil1 = NRF24L01+ Breakout Board
  PIR1 = PIR sensor

nets:
  VCC: U2.pin1, BAT1.+, Bauteil1.VCC, PIR1.VDD
  N1: U2.pin7, Bauteil1.MISO
  N2: U2.pin8, Bauteil1.MOSI
  N3: U2.pin9, Bauteil1.SCK
  N4: U2.pin10, Bauteil1.CS
  N5: U2.pin11, Bauteil1.CE
  N6: U2.pin13, R1.Pin_1, PIR1.SIG
  GND: U2.pin14, R1.Pin_0, BAT1.-, Bauteil1.GND, PIR1.GND

custom parts:
  ATTiny84: Atmel ATTiny84 processor. 8 ADC pins, 4 PWM pins. Available in either 10MHz or 20MHz. The last 2 pin numbers refer to arduino. D6 = Arduino 6, A6 = Arduino A6 example: PA6 (SDA/MOSI/OC1A/DI/AD6/PCINT6/D6/A6) NOTE: This part is diagrammed to suit the MIT HLT ATTiny84 core at https://github.com/damellis/attiny/
